# Fritzing sketch diagram (saved by Fritzing 0.9.3b)

parts:
  Part1 = Arduino Uno (Rev3) - ICSP
  U1 = ESP8266 NodeMCU LoLin module
  JP1 = Header 2 [package=r_sw_th]
  JP2 = Header 2 [package=r_sw_th]

nets:
  N1: Part1.A0, JP1.1
  N2: Part1.A1, JP2.1
  N3: Part1.D1/TX, U1.RX
  N4: Part1.5V, JP1.2

custom parts:
  ESP8266 NodeMCU LoLin module: ESP8266 based NodeMCU
